// Logisim project TP2.circ as structural Verilog: 3 circuits, main circuit main
module Additionneur (
  input  A1,
  input  B1,
  input  C1,
  output S1,
  output R1
);

  wire nand_1_out, nand_2_out, xor_1_out;

  xor xor_1 (xor_1_out, A1, B1);
  xor xor_2 (S1, xor_1_out, C1);
  nand nand_1 (nand_1_out, C1, xor_1_out);
  nand nand_2 (nand_2_out, A1, B1);
  nand nand_3 (R1, nand_1_out, nand_2_out);
endmodule

module Demi_Additionneur (
  input  A0,
  input  B0,
  output S0,
  output R0
);

  wire nand_1_out, nand_2_out, nand_3_out, nand_4_out, nand_5_out;

  nand nand_1 (nand_1_out, A0, A0);
  nand nand_2 (nand_2_out, B0, B0);
  nand nand_3 (nand_3_out, A0, B0);
  nand nand_4 (nand_4_out, nand_1_out, B0);
  nand nand_5 (nand_5_out, A0, nand_2_out);
  nand nand_6 (R0, nand_3_out, nand_3_out);
  nand nand_7 (S0, nand_4_out, nand_5_out);
endmodule

module main (
  input  A0,
  input  B0,
  input  A1,
  input  B1
);

  wire additionneur_1_r1, additionneur_1_s1, demi_additionneur_1_r0, demi_additionneur_1_s0;

  Demi_Additionneur demi_additionneur_1 (.A0(A0), .B0(B0), .S0(demi_additionneur_1_s0), .R0(demi_additionneur_1_r0));
  // Probe on demi_additionneur_1_s0
  Additionneur additionneur_1 (
    .A1(A1), .B1(B1), .C1(demi_additionneur_1_r0), .S1(additionneur_1_s1), .R1(additionneur_1_r1));
  // Probe on additionneur_1_s1
  // Probe on additionneur_1_r1
endmodule
