// Logisim project TP3_1.circ as structural Verilog: 1 circuit, main circuit main
module main (
);

  wire and_1_out, clk_out, j_k_ff_1_q, j_k_ff_2_q, j_k_ff_3_q, j_k_ff_3_qn;

  Clock sysclk ();  // open: out
  Clock clk (.out(clk_out));
  J_K_Flip_Flop #(.trigger("falling")) j_k_ff_1 (
    .J(j_k_ff_3_qn), .K(1'b1), .clk(clk_out), .Q(j_k_ff_1_q));  // open: Qn, preset, reset
  // Probe on j_k_ff_1_q
  J_K_Flip_Flop #(.trigger("falling")) j_k_ff_2 (
    .J(1'b1), .K(1'b1), .clk(j_k_ff_1_q), .Q(j_k_ff_2_q));  // open: Qn, preset, reset
  and and_1 (and_1_out, j_k_ff_1_q, j_k_ff_2_q);
  // Probe on j_k_ff_2_q
  J_K_Flip_Flop #(.trigger("falling")) j_k_ff_3 (
    .J(and_1_out), .K(1'b1), .clk(clk_out), .Q(j_k_ff_3_q), .Qn(j_k_ff_3_qn));  // open: preset, reset
  // Probe on j_k_ff_3_q
endmodule
