// Logisim project TP3_2.circ as structural Verilog: 1 circuit, main circuit main
module main (
);

  wire and_1_out, clk, j_k_ff_1_q, j_k_ff_2_q, j_k_ff_3_q, j_k_ff_4_q;

  Clock sysclk ();  // open: out
  Clock u_clk (.out(clk));
  J_K_Flip_Flop #(.trigger("falling")) j_k_ff_1 (
    .J(1'b1), .K(1'b1), .clk(clk), .Q(j_k_ff_1_q), .reset(and_1_out));  // open: Qn, preset
  // Probe on j_k_ff_1_q
  J_K_Flip_Flop #(.trigger("falling")) j_k_ff_2 (
    .J(1'b1), .K(1'b1), .clk(j_k_ff_1_q), .Q(j_k_ff_2_q), .reset(and_1_out));  // open: Qn, preset
  and and_1 (and_1_out, j_k_ff_4_q, j_k_ff_2_q);
  // Probe on j_k_ff_2_q
  J_K_Flip_Flop #(.trigger("falling")) j_k_ff_3 (
    .J(1'b1), .K(1'b1), .clk(j_k_ff_2_q), .Q(j_k_ff_3_q), .reset(and_1_out));  // open: Qn, preset
  // Probe on j_k_ff_3_q
  J_K_Flip_Flop #(.trigger("falling")) j_k_ff_4 (
    .J(1'b1), .K(1'b1), .clk(j_k_ff_3_q), .Q(j_k_ff_4_q), .reset(and_1_out));  // open: Qn, preset
  // Probe on j_k_ff_4_q
endmodule
