// Logisim project TP3_4.circ as structural Verilog: 1 circuit, main circuit main
module main (
  output Qb,
  output Qa,
  output Qc
);

  wire button_1_out, button_2_out, clk_out, j_k_ff_1_qn, j_k_ff_2_qn;

  Clock sysclk ();  // open: out
  Clock clk (.out(clk_out));
  J_K_Flip_Flop j_k_ff_1 (
    .J(j_k_ff_2_qn), .K(Qb), .clk(clk_out), .Q(Qa), .Qn(j_k_ff_1_qn), .preset(button_1_out),
    .reset(button_2_out));
  J_K_Flip_Flop j_k_ff_2 (
    .J(Qa), .K(j_k_ff_1_qn), .clk(clk_out), .Q(Qb), .Qn(j_k_ff_2_qn), .preset(button_1_out),
    .reset(button_2_out));
  J_K_Flip_Flop j_k_ff_3 (
    .J(Qb), .K(Qb), .clk(clk_out), .Q(Qc), .preset(button_1_out), .reset(button_2_out));  // open: Qn
  Button button_1 (.out(button_1_out));
  Button button_2 (.out(button_2_out));
endmodule
