// Logisim project TP3_5.circ as structural Verilog: 1 circuit, main circuit main
module main (
  output Qa,
  output Qb,
  output Qc,
  output Qd
);

  wire and_1_out, and_2_out, button_1_out, clk_out, not_1_out;

  Clock clk (.out(clk_out));
  Clock sysclk ();  // open: out
  not not_1 (not_1_out, 1'b1);
  J_K_Flip_Flop j_k_ff_1 (
    .J(1'b1), .K(1'b1), .clk(clk_out), .Q(Qa), .preset(not_1_out), .reset(button_1_out));  // open: Qn
  J_K_Flip_Flop j_k_ff_2 (.J(Qa), .K(Qa), .clk(clk_out), .Q(Qb), .preset(not_1_out), .reset(button_1_out));  // open: Qn
  Button button_1 (.out(button_1_out));
  and and_1 (and_1_out, Qa, Qb);
  J_K_Flip_Flop j_k_ff_3 (
    .J(and_1_out), .K(and_1_out), .clk(clk_out), .Q(Qc), .preset(not_1_out), .reset(button_1_out));  // open: Qn
  and and_2 (and_2_out, and_1_out, Qc);
  J_K_Flip_Flop j_k_ff_4 (
    .J(and_2_out), .K(and_2_out), .clk(clk_out), .Q(Qd), .preset(not_1_out), .reset(button_1_out));  // open: Qn
endmodule
